# Fritzing sketch buildwatch-fritzing (saved by Fritzing 0.7.12b)
breadboards: 2

parts:
  LED_R2 = LED - 5mm [color="Red (633nm)" part_number=511-745 package="5 mm [THT]"]
  LED_Y2 = LED - 5mm [color="Yellow (592nm)" part_number=511-746 package="5 mm [THT]"]
  LED_G2 = LED - 5mm [color="Green (555nm)" part_number=511-697 package="5 mm [THT]"]
  Arduino1 = Arduino Nano v3.0
  LED_R1 = LED - 5mm [color="Red (633nm)" part_number=511-745 package="5 mm [THT]"]
  LED_Y1 = LED - 5mm [color="Yellow (592nm)" part_number=511-746 package="5 mm [THT]"]
  LED_G1 = LED - 5mm [color="Green (555nm)" part_number=511-697 package="5 mm [THT]"]
  R4 = Resistor [tolerance=±5% resistance=150 package=THT]
  R5 = Resistor [tolerance=±5% resistance=150 package=THT]
  R6 = Resistor [tolerance=±5% resistance=100 package=THT]
  R1 = Resistor [tolerance=±5% resistance=150 package=THT]
  R2 = Resistor [tolerance=±5% resistance=150 package=THT]
  R3 = Resistor [tolerance=±5% resistance=100 package=THT]

nets:
  N1: LED_R2.cathode, LED_Y2.cathode, LED_G2.cathode, Arduino1.GND, LED_R1.cathode, LED_Y1.cathode, LED_G1.cathode
  N2: LED_R2.anode, R5.Pin_0
  N3: LED_Y2.anode, R4.Pin_0
  N4: LED_G2.anode, R6.Pin_0
  N5: Arduino1.D3, R6.Pin_1
  N6: Arduino1.D5, R4.Pin_1
  N7: Arduino1.D6, R5.Pin_1
  N8: Arduino1.D9, R3.Pin_0
  N9: Arduino1.D10, R2.Pin_0
  N10: Arduino1.D11, R1.Pin_0
  N11: LED_R1.anode, R1.Pin_1
  N12: LED_Y1.anode, R2.Pin_1
  N13: LED_G1.anode, R3.Pin_1
